// Digital circuit CD4511.dig as structural Verilog
// BCD to 7-segment decoder
module CD4511 (
  input  A,
  input  B,
  input  C,
  input  D,
  input  LE,
  input  nLT,
  input  VCC,
  input  GND,
  input  nBL,
  output a_2,
  output b_2,
  output c_2,
  output d_2,
  output e,
  output f,
  output g
);

  wire [3:0] and_1_out, and_2_out, nor_1_out, nor_2_out, not_2_out;
  wire [3:3] not_1_out;
  wire [6:0] multiplexer_1_out, rom_1_d;

  PowerSupply powersupply_1 (.VDD(VCC), .GND(GND));
  not not_1 (not_1_out[3], LE);
  assign not_2_out = ~{D, C, B, A};  // Not not_2, 4 bits wide
  assign and_1_out = not_2_out & {4{not_1_out[3]}};  // And and_1, 4 bits wide
  assign and_2_out = {4{not_1_out[3]}} & {D, C, B, A};  // And and_2, 4 bits wide
  assign nor_1_out = ~(and_1_out | nor_2_out);  // NOr nor_1, 4 bits wide
  assign nor_2_out = ~(nor_1_out | and_2_out);  // NOr nor_2, 4 bits wide
  ROM #(.AddrBits(4), .Bits(7)) rom_1 (.A(nor_1_out), .sel(1'b1), .D(rom_1_d));
  Multiplexer #(.Bits(7)) multiplexer_1 (.sel(nBL), .in_0({7{1'b0}}), .in_1(rom_1_d), .out(multiplexer_1_out));
  Multiplexer #(.Bits(7)) multiplexer_2 (
    .sel(nLT), .in_0({7{1'b1}}), .in_1(multiplexer_1_out), .out({a_2, b_2, c_2, d_2, e, f, g}));

  // Notes on the sheet:
  //   A: Bit 0, pin 7
  //   B: Bit 1, pin 1
  //   C: Bit 2, pin 2
  //   D: Bit 3, pin 6
  //   LE: Letch Enable, pin 5
  //   a_2: pin 13
  //   b_2: pin 12
  //   c_2: pin 11
  //   d_2: pin 10
  //   e: pin 9
  //   f: pin 15
  //   g: pin 14
  //   nLT: lamp test, pin 3
  //   VCC: pin 16, default 1
  //   GND: pin 8
  //   nBL: Blank Output, pin 4
  //   contents of rom_1 (hex, n*v repeats v):
  //   7e,30,6d,79,33,5b,1f,70,7f,73
endmodule
